// Logisim project Mininal_MIPS_datapath.circ as structural Verilog: 2 circuits, main circuit main
module main (
  input  in_1
);

  wire and_1_out, button_1_out, clock_1_out, comparator_1_eq;
  wire [3:0] alucontrolunit_1_alufunc;
  wire [4:0] multiplexer_2_out;
  wire [8:0] rom_1_data;
  wire [31:0] adder_1_out, adder_2_out, bit_extender_1_out, mips_alu_1_p4, mips_ram_1_p4,
       mipsprogramrom_1_p2, multiplexer_1_out, multiplexer_3_out, register_1_q, registerfile_1_p1,
       registerfile_1_p6, registerfile_1_p7, shifter_1_out;

  Adder #(.width(32)) adder_1 (.a(register_1_q), .b(32'h4), .out(adder_1_out));  // open: cin, cout
  Button button_1 (.out(button_1_out));
  Multiplexer #(.width(32), .enable("false")) multiplexer_1 (
    .in0(adder_1_out), .in1(adder_2_out), .out(multiplexer_1_out), .sel(and_1_out));
  Register #(.width(32), .trigger("falling")) register_1 (
    .D(multiplexer_1_out), .en(in_1), .clk(clock_1_out), .Q(register_1_q), .clr(button_1_out));
  Clock clock_1 (.out(clock_1_out));
  Adder #(.width(32)) adder_2 (.a(adder_1_out), .b(shifter_1_out), .out(adder_2_out));  // open: cin, cout
  // MIPSProgramROM mipsprogramrom_1: pin names not known; wires that end beside it: register_1_q, mipsprogramrom_1_p2, clock_1_out
  ROM #(.addrWidth(6), .dataWidth(9)) rom_1 (.addr(mipsprogramrom_1_p2[31:26]), .data(rom_1_data));
  Multiplexer #(.width(5), .enable("false")) multiplexer_2 (
    .in0(mipsprogramrom_1_p2[20:16]), .in1(mipsprogramrom_1_p2[15:11]), .out(multiplexer_2_out),
    .sel(rom_1_data[8]));
  // RegisterFile #(.trigger("falling")) registerfile_1: pin names not known; wires that end beside it: registerfile_1_p1, rom_1_data[5], multiplexer_2_out, mipsprogramrom_1_p2[25:21], mipsprogramrom_1_p2[20:16], registerfile_1_p6, registerfile_1_p7
  assign bit_extender_1_out = {{16{mipsprogramrom_1_p2[15]}}, mipsprogramrom_1_p2[15:0]};  // Bit_Extender bit_extender_1
  Multiplexer #(.width(32), .enable("false")) multiplexer_3 (
    .in0(registerfile_1_p7), .in1(bit_extender_1_out), .out(multiplexer_3_out), .sel(rom_1_data[7]));
  ALUControlUnit alucontrolunit_1 (
    .ALUOp(rom_1_data[1:0]), .funccode(mipsprogramrom_1_p2[5:0]), .Opcode(mipsprogramrom_1_p2[31:26]),
    .ALUfunc(alucontrolunit_1_alufunc));
  // Mips_ALU mips_alu_1: pin names not known; wires that end beside it: registerfile_1_p6, multiplexer_3_out, alucontrolunit_1_alufunc, mips_alu_1_p4, registerfile_1_p7
  Comparator #(.width(32)) comparator_1 (
    .a(registerfile_1_p6), .b(multiplexer_3_out), .eq(comparator_1_eq));  // open: gt, lt
  Shifter #(.width(32)) shifter_1 (.in(bit_extender_1_out), .\dist (5'b00010), .out(shifter_1_out));
  and and_1 (and_1_out, rom_1_data[2], comparator_1_eq);
  // MIPS_RAM #(.addrWidth(24)) mips_ram_1: pin names not known; wires that end beside it: mips_alu_1_p4[23:0], rom_1_data[3], rom_1_data[4], mips_ram_1_p4
  Multiplexer #(.width(32), .enable("false")) multiplexer_4 (
    .in0(mips_alu_1_p4), .in1(mips_ram_1_p4), .out(registerfile_1_p1), .sel(rom_1_data[6]));

  // Notes on the sheet:
  //   contents of mipsprogramrom_1 (hex, n*v repeats v):
  //   addiu $6, $0, 3 # $5 = 3 addu $7, $4, $6 # $7 = $4 + $6 beq $3, $0, else # branch to else if $3 == 0
  //   addiu $3, $3, 0x7 # $3 = $3 + 0x7 andi $4, $3, 1 # $4 = $3 && (0000 0000 0000 0000 0000 0000 0000
  //   0001) else: addiu $5, $4, 0 # bring $4 to $5
  //   contents of rom_1 (hex, n*v repeats v):
  //   122 0 0 0 5 4*0 a3 0 0 a3
endmodule

module ALUControlUnit (
  input  [1:0] ALUOp,
  input  [5:0] funccode,
  input  [5:0] Opcode,
  output [3:0] ALUfunc
);

  wire [3:0] rom_1_data, rom_2_data;

  ROM #(.addrWidth(6), .dataWidth(4)) rom_1 (.addr(funccode), .data(rom_1_data));
  ROM #(.addrWidth(6), .dataWidth(4)) rom_2 (.addr(Opcode), .data(rom_2_data));
  Multiplexer #(.select(2), .width(4), .enable("false")) multiplexer_1 (
    .in0(4'b0010), .in2(rom_1_data), .in3(rom_2_data), .out(ALUfunc), .sel(ALUOp));  // open: in1

  // Notes on the sheet:
  //   contents of rom_1 (hex, n*v repeats v):
  //   33*0 2 0 0 4
  //   contents of rom_2 (hex, n*v repeats v):
  //   9*0 2 0 8 8
endmodule
