// Logisim project teach_circ.circ as structural Verilog: 2 circuits, main circuit main
module main (
  output [3:0] out_1
);

  wire [3:0] register_1_q;

  Register #(.width(4), .trigger("falling")) register_1 (.Q(register_1_q));  // open: D, en, clk, clr
  ROM #(.addrWidth(4), .dataWidth(12)) rom_1 (.addr(register_1_q));  // open: data
  ALU alu_1 (.ALUResult(out_1));  // open: A, B, SelectBit
  Hex_Digit_Display hex_digit_display_1 (.value(out_1));  // open: dp
endmodule

module ALU (
  input  [3:0] A,
  input  [3:0] B,
  input  [2:0] SelectBit,
  output [3:0] ALUResult
);

  wire comparator_1_eq, comparator_1_gt, comparator_1_lt;
  wire [3:0] adder_1_out, and_1_out, bit_extender_1_out, bit_extender_2_out, bit_extender_3_out, or_1_out,
       subtractor_1_out, xor_1_out;

  Adder #(.width(4)) adder_1 (.a(A), .b(B), .out(adder_1_out));  // open: cin, cout
  Subtractor #(.width(4)) subtractor_1 (.a(A), .b(B), .out(subtractor_1_out));  // open: bin, bout
  Comparator #(.width(4), .mode("unsigned")) comparator_1 (
    .a(A), .b(B), .gt(comparator_1_gt), .eq(comparator_1_eq), .lt(comparator_1_lt));
  assign and_1_out = A & B;  // AND_Gate and_1, 4 bits wide
  assign or_1_out = A | B;  // OR_Gate or_1, 4 bits wide
  assign xor_1_out = A ^ B;  // XOR_Gate xor_1, 4 bits wide
  assign bit_extender_1_out = {{3{1'b0}}, comparator_1_eq};  // Bit_Extender bit_extender_1
  assign bit_extender_2_out = {{3{1'b0}}, comparator_1_gt};  // Bit_Extender bit_extender_2
  assign bit_extender_3_out = {{3{1'b0}}, comparator_1_lt};  // Bit_Extender bit_extender_3
  Multiplexer #(.select(3), .width(4), .enable("false")) multiplexer_1 (
    .in0(adder_1_out), .in1(subtractor_1_out), .in2(and_1_out), .in3(or_1_out), .in4(xor_1_out),
    .in5(bit_extender_1_out), .in6(bit_extender_2_out), .in7(bit_extender_3_out), .out(ALUResult),
    .sel(SelectBit));
endmodule
